# Fritzing sketch WeatherStation-wiring (saved by Fritzing 0.9.3b)
breadboards: 1

parts:
  WeMos_D1_Mini1 = WeMos D1 Mini
  Part3 = Adafruit BMP180  # not connected
  DHT1 = DHT22 Humidity and Temperature Sensor
  R1 = Photocell (LDR) [package=THT]
  R2 = Resistor [tolerance=±5% resistance=3.3k package="2512 [SMD]"]
  R3 = Resistor [tolerance=±5% resistance=10k package="2512 [SMD]"]
  D1 = Schottky Diode [part_number=BAT43 package="Melf DO-213 AB [SMD]"]  # not connected
  U2 = Voltage Regulator - Variable [package="TO220 [THT]"]
  R5 = Trimmer Potentiometer [maximum_resistance=10kΩ package=THT]
  R6 = Resistor [tolerance=±5% resistance=3.3k package="2512 [SMD]"]

nets:
  3V3: WeMos_D1_Mini1.3V3, DHT1.VDD, R1.pin_1, R3.Pin_0
  N1: WeMos_D1_Mini1.A0, R1.pin_0, R2.Pin_0
  N2: WeMos_D1_Mini1.D0, WeMos_D1_Mini1.RST
  N3: WeMos_D1_Mini1.D5, DHT1.DATA, R3.Pin_1
  N4: WeMos_D1_Mini1.G, DHT1.GND, R2.Pin_1
  N5: U2.OUT, R6.Pin_1
  N6: R5.leg2, R6.Pin_0

custom parts:
  Adafruit BMP180: This precision sensor from Bosch is the best low-cost sensing solution for measuring barometric pressure and temperature. Because pressure changes with altitude you can also use it as an altimeter! The sensor is soldered onto a PCB with a 3.3V regulator, I2C level shifter and pull-up resistors on the I2C pins. The BMP180 is the next-generation of sensors from Bosch, and replaces the BMP085.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
