# Fritzing sketch wiring-schematic (saved by Fritzing 0.9.5d)
breadboards: 1

parts:
  WeMos_D1_Mini1 = WeMos D1 Mini
  JACK1 = 2.1mm Barrel Jack with Terminal Block
  NEOPIXEL1 = Neopixel Strip -- Black (60/m) [part_number=1461]

nets:
  5V: WeMos_D1_Mini1.5V, JACK1.POS, NEOPIXEL1.+5V
  N1: WeMos_D1_Mini1.G, JACK1.NEG, NEOPIXEL1.GND
  N2: WeMos_D1_Mini1.RX, NEOPIXEL1.DI

notes:
  Wiring schematic WeMos D1 Mini with WS2812, 5VDC power supply

custom parts:
  Neopixel Strip -- Black (60/m): Neopixel Strip, Black, 60 pixels per meter.
